// Digital circuit 8-Bit Memory.dig as structural Verilog
module _8_Bit_Memory (
  input  [2:0] Address_Pin,
  input  Clock,
  input  [7:0] Data_Input,
  input  [1:0] CTRL_BUS,
  output [7:0] Data_Ouput
);

  wire and_1_out, and_2_out, and_3_out, and_4_out, and_5_out, and_6_out, and_7_out, and_8_out,
       decoder_1_out_0, decoder_1_out_1, decoder_1_out_2, decoder_1_out_3, decoder_1_out_4, decoder_1_out_5,
       decoder_1_out_6, decoder_1_out_7;
  wire [7:0] _8_bit_mem_imp___in_class_1_output, _8_bit_mem_imp___in_class_2_output,
       _8_bit_mem_imp___in_class_3_output, _8_bit_mem_imp___in_class_4_output,
       _8_bit_mem_imp___in_class_5_output, _8_bit_mem_imp___in_class_6_output,
       _8_bit_mem_imp___in_class_7_output, _8_bit_mem_imp___in_class_8_output;

  Decoder #(.Selector_Bits(3)) decoder_1 (
    .sel(Address_Pin), .out_0(decoder_1_out_0), .out_1(decoder_1_out_1), .out_2(decoder_1_out_2),
    .out_3(decoder_1_out_3), .out_4(decoder_1_out_4), .out_5(decoder_1_out_5), .out_6(decoder_1_out_6),
    .out_7(decoder_1_out_7));
  and and_1 (and_1_out, Clock, decoder_1_out_0);
  and and_2 (and_2_out, Clock, decoder_1_out_1);
  and and_3 (and_3_out, Clock, decoder_1_out_2);
  and and_4 (and_4_out, Clock, decoder_1_out_3);
  and and_5 (and_5_out, Clock, decoder_1_out_4);
  and and_6 (and_6_out, Clock, decoder_1_out_5);
  and and_7 (and_7_out, Clock, decoder_1_out_6);
  and and_8 (and_8_out, Clock, decoder_1_out_7);
  _8_bit_Mem_Imp___In_Class _8_bit_mem_imp___in_class_1 (
    .CLK(and_1_out), .Input(Data_Input), .CTRL_Input(CTRL_BUS), .Output(_8_bit_mem_imp___in_class_1_output));
  _8_bit_Mem_Imp___In_Class _8_bit_mem_imp___in_class_2 (
    .CLK(and_2_out), .Input(Data_Input), .CTRL_Input(CTRL_BUS), .Output(_8_bit_mem_imp___in_class_2_output));
  _8_bit_Mem_Imp___In_Class _8_bit_mem_imp___in_class_3 (
    .CLK(and_3_out), .Input(Data_Input), .CTRL_Input(CTRL_BUS), .Output(_8_bit_mem_imp___in_class_3_output));
  _8_bit_Mem_Imp___In_Class _8_bit_mem_imp___in_class_4 (
    .CLK(and_4_out), .Input(Data_Input), .CTRL_Input(CTRL_BUS), .Output(_8_bit_mem_imp___in_class_4_output));
  _8_bit_Mem_Imp___In_Class _8_bit_mem_imp___in_class_5 (
    .CLK(and_5_out), .Input(Data_Input), .CTRL_Input(CTRL_BUS), .Output(_8_bit_mem_imp___in_class_5_output));
  _8_bit_Mem_Imp___In_Class _8_bit_mem_imp___in_class_6 (
    .CLK(and_6_out), .Input(Data_Input), .CTRL_Input(CTRL_BUS), .Output(_8_bit_mem_imp___in_class_6_output));
  _8_bit_Mem_Imp___In_Class _8_bit_mem_imp___in_class_7 (
    .CLK(and_7_out), .Input(Data_Input), .CTRL_Input(CTRL_BUS), .Output(_8_bit_mem_imp___in_class_7_output));
  _8_bit_Mem_Imp___In_Class _8_bit_mem_imp___in_class_8 (
    .CLK(and_8_out), .Input(Data_Input), .CTRL_Input(CTRL_BUS), .Output(_8_bit_mem_imp___in_class_8_output));
  Multiplexer #(.Bits(8), .Selector_Bits(3)) multiplexer_1 (
    .sel(Address_Pin), .in_0(_8_bit_mem_imp___in_class_1_output), .in_1(_8_bit_mem_imp___in_class_2_output),
    .in_2(_8_bit_mem_imp___in_class_3_output), .in_3(_8_bit_mem_imp___in_class_4_output),
    .in_4(_8_bit_mem_imp___in_class_5_output), .in_5(_8_bit_mem_imp___in_class_6_output),
    .in_6(_8_bit_mem_imp___in_class_7_output), .in_7(_8_bit_mem_imp___in_class_8_output), .out(Data_Ouput));
endmodule
