// Digital circuit 8-bit Mem Imp - In Class.dig as structural Verilog
module _8_bit_Mem_Imp___In_Class (
  input  CLK,
  input  [7:0] Input,
  input  [1:0] CTRL_Input,
  output [7:0] Output
);

  wire [7:0] multiplexer_1_out;

  Multiplexer #(.Bits(8), .Selector_Bits(2)) multiplexer_1 (
    .sel(CTRL_Input), .in_0(Output), .in_1(Input), .in_2({8{1'b0}}), .in_3({8{1'b1}}), .out(multiplexer_1_out));
  D_FF d_ff_1 (.D(multiplexer_1_out[7]), .C(CLK), .Q(Output[7]));  // open: nQ
  D_FF d_ff_2 (.D(multiplexer_1_out[6]), .C(CLK), .Q(Output[6]));  // open: nQ
  D_FF d_ff_3 (.D(multiplexer_1_out[5]), .C(CLK), .Q(Output[5]));  // open: nQ
  D_FF d_ff_4 (.D(multiplexer_1_out[4]), .C(CLK), .Q(Output[4]));  // open: nQ
  D_FF d_ff_5 (.D(multiplexer_1_out[3]), .C(CLK), .Q(Output[3]));  // open: nQ
  D_FF d_ff_6 (.D(multiplexer_1_out[2]), .C(CLK), .Q(Output[2]));  // open: nQ
  D_FF d_ff_7 (.D(multiplexer_1_out[1]), .C(CLK), .Q(Output[1]));  // open: nQ
  D_FF d_ff_8 (.D(multiplexer_1_out[0]), .C(CLK), .Q(Output[0]));  // open: nQ

  // Notes on the sheet:
  //   CTRL_Input: 00 - Load
  //   01 - Store
  //   10 - Clear
  //   11 - Set
endmodule
