// Digital circuit 8-bit-Processor.dig as structural Verilog
module _8_bit_Processor (
  input  [7:0] InstrMem_input,
  input  [1:0] InstrMem_ctrl,
  input  clk,
  output [7:0] IR_output,
  output Inst_Fetch,
  output Instr_Decode,
  output Instr_Exec,
  output Write_Back,
  output [1:0] IR_ctrl,
  output [2:0] Program_Counter,
  output [7:0] RegFile_ctrl,
  output [7:0] ALU_output
);

  wire [7:0] _8_bit_memory_1_data_ouput, multiplexer_2_out, multiplexer_4_out, registerfile_1_read_data_1,
       registerfile_1_read_data_2;
  wire [7:3] _8_bit_programcounter_1_output;

  _8_bit_ProgramCounter _8_bit_programcounter_1 (
    .CLK(clk), .INC_by(8'h1), .CTRL_Input({1'b0, Write_Back}),
    .Output({_8_bit_programcounter_1_output, Program_Counter}));
  _8_Bit_Memory _8_bit_memory_1 (
    .Address_Pin(Program_Counter), .Clock(clk), .Data_Input(InstrMem_input), .CTRL_BUS(InstrMem_ctrl),
    .Data_Ouput(_8_bit_memory_1_data_ouput));
  Multiplexer multiplexer_1 (.sel(InstrMem_ctrl[0]), .in_0(Inst_Fetch), .in_1(1'b0), .out(IR_ctrl[0]));
  ControlUnit controlunit_1 (
    .CLK(clk), .Instr_Fetch(Inst_Fetch), .Instr_Decode(Instr_Decode), .Instr_Execute(Instr_Exec),
    .Write_Back(Write_Back));
  _8_bit_IR _8_bit_ir_1 (.Input(_8_bit_memory_1_data_ouput), .CTRL({1'b0, IR_ctrl[0]}), .CLK(clk), .Output(IR_output));
  Multiplexer #(.Selector_Bits(2), .Bits(8)) multiplexer_2 (
    .sel(IR_output[4:3]), .in_0(8'h1), .in_1(8'h4), .in_2(8'h10), .in_3(8'h40), .out(multiplexer_2_out));
  Multiplexer #(.Bits(8)) multiplexer_3 (
    .sel(Write_Back), .in_0({8{1'b0}}), .in_1(multiplexer_2_out), .out(RegFile_ctrl));
  RegisterFile registerfile_1 (
    .clk(clk), .Read_Register_1(IR_output[4:3]), .Read_Register_2(IR_output[2:1]), .Write_Data(ALU_output),
    .Write_Register(IR_output[4:3]), .CTRL(RegFile_ctrl), .Read_Data_1(registerfile_1_read_data_1),
    .Read_Data_2(registerfile_1_read_data_2));
  Multiplexer #(.Bits(8)) multiplexer_4 (
    .sel(IR_output[0]), .in_0(registerfile_1_read_data_1), .in_1({{6{1'b0}}, IR_output[2:1]}),
    .out(multiplexer_4_out));
  ALU alu_1 (
    .A(multiplexer_4_out), .S_1_S_0_Carry_in(IR_output[7:5]), .B(registerfile_1_read_data_2),
    .Output(ALU_output));  // open: Status

  assign IR_ctrl[1] = 1'b0;
endmodule

/* Test case:
# =========================================================
# 8-bit processor test
#
# Signals:
#   clk Program_Counter InstrMem_input InstrMem_ctrl
#   IR_output IR_ctrl Write_Back ALU_output
#
# Instruction format:
#   [ opcode(3) | op1(2) | op2(2) | type(1) ]
#
# opcode = ALU control bits = S1 S0 Cin
#
# ALU control / opcode meanings:
#   000 = A + B                  (ADD)
#   001 = A + B + 1              (ADD with carry)
#   010 = A + B̅                 (SUB with borrow)
#   011 = A + B̅ + 1             (SUB)
#   100 = A                      (TRANSFER A)
#   101 = A + 1                  (INCREMENT A)
#   110 = A - 1                  (DECREMENT A)
#   111 = A                      (TRANSFER A)
#
# Register encoding:
#   00 = R0
#   01 = R1
#   10 = R2
#   11 = R3
#
# Type bit:
#   0 = R-type
#   1 = I-type
#
# Notes:
# - In R-type, op1 is A and destination, op2 selects register B.
# - In I-type, op2 is the 2-bit immediate value.
# - TRANSFER A should be encoded as I-type here, with op2 filled
#   as an immediate field.
# - Registers are assumed to start at 0.
#
# Program:
#   0: INC   R1        ; R1 = 1
#   1: INC   R1        ; R1 = 2
#   2: ADDI  R2, 3     ; R2 = 3
#   3: ADD   R2, R1    ; R2 = 5
#   4: SUB   R2, R1    ; R2 = 3
#   5: SUBB  R2, R1    ; R2 = 0
#   6: INC   R0        ; R0 = 1
#   7: DEC   R0        ; R0 = 0
#   8: TRANSFER A R2   ; I-type, imm=01, R2 stays 0
#   9: TRANSFER A R2   ; I-type, imm=10, R2 stays 0
# =========================================================

clk Program_Counter InstrMem_input InstrMem_ctrl IR_output IR_ctrl Write_Back ALU_output

# ---------------------------------------------------------
# settle
# ---------------------------------------------------------
#repeat(10) C X 0 0 X X X X

# ---------------------------------------------------------
# program instruction memory
# ---------------------------------------------------------

# ---------------------------------------------------------
# addr 0 : 168 = INC R1
#
# 168 = 0xA8 = 10101000
#
# Breakdown:
#   opcode = 101  -> Increment A
#   op1    = 01   -> R1
#   op2    = 00   -> immediate field present but ignored by INC
#   type   = 0    -> R-type
#
# Meaning:
#   R1 <- R1 + 1
# ---------------------------------------------------------
C X 168 1 X X X X
repeat(3) C X 0 0 X X X X

# ---------------------------------------------------------
# addr 1 : 168 = INC R1
#
# Same instruction again
# Meaning:
#   R1 <- R1 + 1
# ---------------------------------------------------------
C X 168 1 X X X X
repeat(3) C X 0 0 X X X X

C X 168 1 X X X X
repeat(3) C X 0 0 X X X X

C X 168 1 X X X X
repeat(3) C X 0 0 X X X X

# ---------------------------------------------------------
# addr 0 : 168 = INC R2
#
# 176 = 0xA8 = 10110000
#
# Breakdown:
#   opcode = 101  -> Increment A
#   op1    = 10   -> R2
#   op2    = 00   -> immediate field present but ignored by INC
#   type   = 0    -> R-type
#
# Meaning:
#   R2 <- R2 + 1
# ---------------------------------------------------------
C X 176 1 X X X X
repeat(3) C X 0 0 X X X X


C X 176 1 X X X X
repeat(3) C X 0 0 X X X X



# ---------------------------------------------------------
# addr 4 : 114 = SUB R1, R2
#
# 108 = 0x6C = 011 01 10 0
#
# Breakdown:
#   opcode = 011  -> Subtract
#   op1    = 01   -> R2
#   op2    = 10   -> R1
#   type   = 0    -> R-type
#
# Meaning:
#   R2 <- R2 - R1
# ---------------------------------------------------------
C X 108 1 X X X X
repeat(3) C X 0 0 X X X X



# ---------------------------------------------------------
# stop programming
# ---------------------------------------------------------
repeat(2) C X 0 0 X X X X

# ---------------------------------------------------------
# run
# ---------------------------------------------------------
# Expected high-level behavior:
#   R1: 0 -> 1 -> 2
#   R2: 0 -> 3 -> 5 -> 3 -> 0 -> 0 -> 0
#   R0: 0 -> 1 -> 0
# ---------------------------------------------------------
repeat(40) C X 0 0 X X X X
*/
