// Digital circuit 8-bit_Adder.dig as structural Verilog
module _8_bit_Adder (
  input  [7:0] A,
  input  [7:0] B,
  input  Carry_in,
  output [7:0] Sum,
  output Carry_out
);

  wire hw1_full_adder_1_p3, hw1_full_adder_2_p3, hw1_full_adder_3_p3, hw1_full_adder_4_p3,
       hw1_full_adder_5_p3, hw1_full_adder_6_p3, hw1_full_adder_7_p3;

  // HW1_Full_Adder hw1_full_adder_1: pin names not known; wires that end beside it: A[7], B[7], hw1_full_adder_1_p3, Sum[7], Carry_out
  // HW1_Full_Adder hw1_full_adder_2: pin names not known; wires that end beside it: A[6], B[6], hw1_full_adder_2_p3, Sum[6], hw1_full_adder_1_p3
  // HW1_Full_Adder hw1_full_adder_3: pin names not known; wires that end beside it: A[5], B[5], hw1_full_adder_3_p3, Sum[5], hw1_full_adder_2_p3
  // HW1_Full_Adder hw1_full_adder_4: pin names not known; wires that end beside it: A[4], B[4], hw1_full_adder_4_p3, Sum[4], hw1_full_adder_3_p3
  // HW1_Full_Adder hw1_full_adder_5: pin names not known; wires that end beside it: A[3], B[3], hw1_full_adder_5_p3, Sum[3], hw1_full_adder_4_p3
  // HW1_Full_Adder hw1_full_adder_6: pin names not known; wires that end beside it: A[2], B[2], hw1_full_adder_6_p3, Sum[2], hw1_full_adder_5_p3
  // HW1_Full_Adder hw1_full_adder_7: pin names not known; wires that end beside it: A[1], B[1], hw1_full_adder_7_p3, Sum[1], hw1_full_adder_6_p3
  // HW1_Full_Adder hw1_full_adder_8: pin names not known; wires that end beside it: A[0], B[0], Carry_in, Sum[0], hw1_full_adder_7_p3
endmodule
