// Digital circuit ALU.dig as structural Verilog
module ALU (
  input  [7:0] A,
  input  [2:0] S_1_S_0_Carry_in,
  input  [7:0] B,
  output [7:0] Output,
  output Status
);

  wire [7:0] multiplexer_1_out, not_1_out, not_2_out;

  assign not_1_out = ~B;  // Not not_1, 8 bits wide
  assign not_2_out = ~{8{1'b0}};  // Not not_2, 8 bits wide
  Multiplexer #(.Selector_Bits(2), .Bits(8)) multiplexer_1 (
    .sel(S_1_S_0_Carry_in[2:1]), .in_0(B), .in_1(not_1_out), .in_2({8{1'b0}}), .in_3(not_2_out),
    .out(multiplexer_1_out));
  _8_bit_full_adder _8_bit_full_adder_1 (
    .A(A), .Y(multiplexer_1_out), .Carry_in(S_1_S_0_Carry_in[0]), .Carry_out(Status), .Sum(Output));
endmodule
