// Digital circuit ControlUnit.dig as structural Verilog
module ControlUnit (
  input  CLK,
  output Instr_Fetch,
  output Instr_Decode,
  output Instr_Execute,
  output Write_Back
);

  D_FF d_ff_1 (.D(Instr_Execute), .C(CLK), .Q(Write_Back));  // open: nQ
  D_FF d_ff_2 (.D(Instr_Decode), .C(CLK), .Q(Instr_Execute));  // open: nQ
  D_FF d_ff_3 (.D(Instr_Fetch), .C(CLK), .Q(Instr_Decode));  // open: nQ
  D_FF #(.Default(1)) d_ff_4 (.D(Write_Back), .C(CLK), .Q(Instr_Fetch));  // open: nQ
endmodule
