// Digital circuit RegisterFile.dig as structural Verilog
module RegisterFile (
  input  clk,
  input  [1:0] Read_Register_1,
  input  [1:0] Read_Register_2,
  input  [7:0] Write_Data,
  input  [1:0] Write_Register,
  input  [7:0] CTRL,
  output [7:0] Read_Data_1,
  output [7:0] Read_Data_2
);

  wire [7:0] demultiplexer_1_out_0, demultiplexer_1_out_1, demultiplexer_1_out_2, demultiplexer_1_out_3,
       R0_output, R1_output, R2_output, R3_output;

  Demultiplexer #(.Bits(8), .Selector_Bits(2)) demultiplexer_1 (
    .sel(Write_Register), .in(Write_Data), .out_0(demultiplexer_1_out_0), .out_1(demultiplexer_1_out_1),
    .out_2(demultiplexer_1_out_2), .out_3(demultiplexer_1_out_3));
  _8_bit_Register R0 (.CLK(clk), .Input(demultiplexer_1_out_0), .CTRL_Input(CTRL[1:0]), .Output(R0_output));
  _8_bit_Register R1 (.CLK(clk), .Input(demultiplexer_1_out_1), .CTRL_Input(CTRL[3:2]), .Output(R1_output));
  _8_bit_Register R2 (.CLK(clk), .Input(demultiplexer_1_out_2), .CTRL_Input(CTRL[5:4]), .Output(R2_output));
  _8_bit_Register R3 (.CLK(clk), .Input(demultiplexer_1_out_3), .CTRL_Input(CTRL[7:6]), .Output(R3_output));
  Multiplexer #(.Bits(8), .Selector_Bits(2)) multiplexer_1 (
    .sel(Read_Register_1), .in_0(R0_output), .in_1(R1_output), .in_2(R2_output), .in_3(R3_output),
    .out(Read_Data_1));
  Multiplexer #(.Selector_Bits(2), .Bits(8)) multiplexer_2 (
    .sel(Read_Register_2), .in_0(R0_output), .in_1(R1_output), .in_2(R2_output), .in_3(R3_output),
    .out(Read_Data_2));
endmodule
